# Fritzing sketch schema (saved by Fritzing 0.7.11b)

parts:
  U1 = Arduino Mega
  Arduino_Ethernet_Shield1 = Arduino Ethernet Shield
  BMP085 = Barometric Pressure Sensor - BMP085 Breakout
  Součástka2 = DeuLigne 1.1 - The Snootlab's LCD shield for Arduino
  DHT11 = Humidity and Temperature Sensor RHT03
  DS18B20 = DS18B20 1-Wire Temperature Sensor Probe Cable
  R1 = Resistor [tolerance=±5% resistance=4.7k package=THT]

nets:
  N1: U1.D10, Arduino_Ethernet_Shield1.SS#5
  N2: U1.D4, Arduino_Ethernet_Shield1.SS#11
  N3: U1.D3, DS18B20.DQ, R1.Pin_1
  N4: U1.D2, DHT11.Data-signal
  VCC: U1.+5V, BMP085.VCC, DHT11.Vcc, DS18B20.VDD, R1.Pin_0
  GND: U1.GND, BMP085.GND, DHT11.GND_2, DS18B20.GND
  N5: U1.A4, BMP085.SDA
  N6: U1.A5, BMP085.SCL
  N7: Arduino_Ethernet_Shield1.MOSI, Součástka2.D4
  N8: Arduino_Ethernet_Shield1.D9, Součástka2.D9
  N9: Arduino_Ethernet_Shield1.D8, Součástka2.D8
  N10: Arduino_Ethernet_Shield1.D7, Součástka2.D7
  N11: Arduino_Ethernet_Shield1.D6, Součástka2.D6
  N12: Arduino_Ethernet_Shield1.D5, Součástka2.D5
